// Logisim project exam3.circ as structural Verilog: 3 circuits, main circuit sold
module sold (
  input  [2:0] in_1,
  output out_2,
  output [1:0] out_3
);

  wire clock_1_out;
  wire [2:0] logic_1_out_3, register_1_q;

  \logic  logic_1 (.in_1(in_1), .in_2(register_1_q), .out_3(logic_1_out_3));  // open: sold, out_5
  Register #(.width(3)) register_1 (.D(logic_1_out_3), .Q(register_1_q), .clk(clock_1_out));  // open: en, clr
  Clock clock_1 (.out(clock_1_out));
  \final  final_1 (.in_1(register_1_q), .in_2(in_1), .sell(out_2), .out_4(out_3));
endmodule

module \logic  (
  input  [2:0] in_1,
  input  [2:0] in_2,
  output [2:0] out_3,
  output sold,
  output [1:0] out_5
);

  wire and_1_out, and_2_out, and_3_out, and_4_out, and_5_out, and_6_out, and_7_out, and_8_out, and_9_out,
       and_10_out, and_11_out, and_12_out, and_13_out, and_14_out, and_15_out, and_16_out, and_17_out,
       and_18_out, and_19_out, not_1_out, not_2_out, not_3_out, not_4_out, not_5_out, not_6_out, not_7_out,
       not_8_out, not_9_out, not_10_out, not_11_out, not_12_out, not_13_out, not_14_out, not_15_out,
       not_16_out, not_17_out, not_18_out, not_19_out, not_20_out, not_21_out, not_22_out, not_23_out,
       not_24_out, not_25_out, not_26_out, not_27_out, not_28_out, not_29_out, not_30_out, not_31_out,
       not_32_out, not_33_out, not_34_out, not_35_out, not_36_out, not_37_out, not_38_out, not_39_out,
       not_40_out, not_41_out, not_42_out, not_43_out, not_44_out, not_45_out, not_46_out, not_47_out,
       not_48_out, not_49_out, not_50_out, not_51_out, not_52_out, not_53_out, not_54_out, not_55_out,
       not_56_out, not_57_out, not_58_out, not_59_out, not_60_out, not_61_out, not_62_out, not_63_out,
       not_64_out, not_65_out, not_66_out, not_67_out, not_68_out, not_69_out, not_70_out, not_71_out,
       not_72_out;

  not not_1 (not_1_out, in_1[2]);
  not not_2 (not_2_out, in_1[1]);
  not not_3 (not_3_out, in_2[2]);
  not not_4 (not_4_out, in_1[2]);
  not not_5 (not_5_out, in_1[0]);
  not not_6 (not_6_out, in_2[2]);
  not not_7 (not_7_out, in_2[0]);
  not not_8 (not_8_out, in_1[1]);
  not not_9 (not_9_out, in_1[0]);
  not not_10 (not_10_out, in_2[2]);
  not not_11 (not_11_out, in_2[1]);
  not not_12 (not_12_out, in_2[0]);
  not not_13 (not_13_out, in_1[2]);
  not not_14 (not_14_out, in_1[1]);
  not not_15 (not_15_out, in_2[2]);
  not not_16 (not_16_out, in_2[1]);
  not not_17 (not_17_out, in_1[2]);
  not not_18 (not_18_out, in_1[1]);
  not not_19 (not_19_out, in_2[2]);
  not not_20 (not_20_out, in_2[0]);
  not not_21 (not_21_out, in_1[2]);
  not not_22 (not_22_out, in_1[0]);
  not not_23 (not_23_out, in_2[2]);
  not not_24 (not_24_out, in_2[1]);
  not not_25 (not_25_out, in_1[2]);
  not not_26 (not_26_out, in_1[1]);
  not not_27 (not_27_out, in_2[2]);
  not not_28 (not_28_out, in_2[0]);
  not not_29 (not_29_out, in_1[2]);
  not not_30 (not_30_out, in_1[0]);
  not not_31 (not_31_out, in_2[2]);
  not not_32 (not_32_out, in_2[1]);
  not not_33 (not_33_out, in_1[2]);
  not not_34 (not_34_out, in_1[1]);
  not not_35 (not_35_out, in_2[1]);
  not not_36 (not_36_out, in_2[0]);
  not not_37 (not_37_out, in_1[2]);
  not not_38 (not_38_out, in_1[0]);
  not not_39 (not_39_out, in_2[2]);
  not not_40 (not_40_out, in_1[2]);
  not not_41 (not_41_out, in_1[0]);
  not not_42 (not_42_out, in_2[1]);
  not not_43 (not_43_out, in_2[0]);
  not not_44 (not_44_out, in_1[1]);
  not not_45 (not_45_out, in_1[0]);
  not not_46 (not_46_out, in_2[2]);
  not not_47 (not_47_out, in_1[1]);
  not not_48 (not_48_out, in_1[0]);
  not not_49 (not_49_out, in_2[2]);
  not not_50 (not_50_out, in_1[1]);
  not not_51 (not_51_out, in_1[0]);
  not not_52 (not_52_out, in_2[1]);
  not not_53 (not_53_out, in_2[0]);
  not not_54 (not_54_out, in_1[1]);
  not not_55 (not_55_out, in_1[0]);
  not not_56 (not_56_out, in_2[2]);
  not not_57 (not_57_out, in_1[1]);
  not not_58 (not_58_out, in_1[0]);
  not not_59 (not_59_out, in_2[1]);
  not not_60 (not_60_out, in_2[0]);
  not not_61 (not_61_out, in_1[2]);
  not not_62 (not_62_out, in_1[0]);
  not not_63 (not_63_out, in_2[1]);
  not not_64 (not_64_out, in_2[0]);
  not not_65 (not_65_out, in_1[1]);
  not not_66 (not_66_out, in_1[0]);
  not not_67 (not_67_out, in_2[2]);
  not not_68 (not_68_out, in_2[0]);
  not not_69 (not_69_out, in_1[1]);
  not not_70 (not_70_out, in_1[0]);
  not not_71 (not_71_out, in_2[1]);
  not not_72 (not_72_out, in_2[0]);
  and and_1 (and_1_out, not_1_out, not_2_out, in_1[0], not_3_out, in_2[1], in_2[0]);
  and and_2 (and_2_out, not_4_out, in_1[1], not_5_out, not_6_out, in_2[1], not_7_out);
  and and_3 (and_3_out, in_1[2], not_8_out, not_9_out, not_10_out, not_11_out, not_12_out);
  and and_4 (and_4_out, not_13_out, not_14_out, in_1[0], not_15_out, not_16_out, in_2[0]);
  and and_5 (and_5_out, not_17_out, not_18_out, in_1[0], not_19_out, in_2[1], not_20_out);
  and and_6 (and_6_out, not_21_out, in_1[1], not_22_out, not_23_out, not_24_out);
  and and_7 (and_7_out, not_25_out, not_26_out, in_1[0], not_27_out, not_28_out);
  and and_8 (and_8_out, not_29_out, in_1[1], not_30_out, not_31_out, not_32_out, in_2[0]);
  and and_9 (and_9_out, not_33_out, not_34_out, in_1[0], in_2[2], not_35_out, not_36_out);
  and and_10 (and_10_out, not_37_out, in_1[1], not_38_out, not_39_out, in_2[1], in_2[0]);
  and and_11 (and_11_out, not_40_out, in_1[1], not_41_out, in_2[2], not_42_out, not_43_out);
  and and_12 (and_12_out, in_1[2], not_44_out, not_45_out, not_46_out, in_2[0]);
  and and_13 (and_13_out, in_1[2], not_47_out, not_48_out, not_49_out, in_2[1]);
  and and_14 (and_14_out, in_1[2], not_50_out, not_51_out, in_2[2], not_52_out, not_53_out);
  and and_15 (and_15_out, in_1[2], not_54_out, not_55_out, not_56_out, in_2[1], in_2[0]);
  and and_16 (and_16_out, in_1[2], not_57_out, not_58_out, in_2[2], not_59_out, not_60_out);
  and and_17 (and_17_out, not_61_out, in_1[1], not_62_out, in_2[2], not_63_out, not_64_out);
  and and_18 (and_18_out, in_1[2], not_65_out, not_66_out, not_67_out, in_2[1], not_68_out);
  and and_19 (and_19_out, in_1[2], not_69_out, not_70_out, in_2[2], not_71_out, not_72_out);
  or or_1 (out_3[2], and_1_out, and_2_out, and_3_out);
  or or_2 (out_3[1], and_4_out, and_5_out, and_6_out);
  or or_3 (out_3[0], and_7_out, and_8_out);
  or or_4 (sold, and_9_out, and_10_out, and_11_out, and_12_out, and_13_out, and_14_out);
  or or_5 (out_5[1], and_15_out, and_16_out);
  or or_6 (out_5[0], and_17_out, and_18_out, and_19_out);
endmodule

module \final  (
  input  [2:0] in_1,
  input  [2:0] in_2,
  output sell,
  output [1:0] out_4
);

  wire and_1_out, and_2_out, and_3_out, and_4_out, and_5_out, and_6_out, and_7_out, and_8_out, and_9_out,
       and_10_out, and_11_out, not_1_out, not_2_out, not_3_out, not_4_out, not_5_out, not_6_out, not_7_out,
       not_8_out, not_9_out, not_10_out, not_11_out, not_12_out, not_13_out, not_14_out, not_15_out,
       not_16_out, not_17_out, not_18_out, not_19_out, not_20_out, not_21_out, not_22_out, not_23_out,
       not_24_out, not_25_out, not_26_out, not_27_out, not_28_out, not_29_out, not_30_out, not_31_out,
       not_32_out, not_33_out, not_34_out, not_35_out, not_36_out, not_37_out, not_38_out, not_39_out,
       not_40_out;

  not not_1 (not_1_out, in_1[2]);
  not not_2 (not_2_out, in_2[1]);
  not not_3 (not_3_out, in_2[0]);
  not not_4 (not_4_out, in_1[2]);
  not not_5 (not_5_out, in_2[1]);
  not not_6 (not_6_out, in_2[0]);
  not not_7 (not_7_out, in_1[2]);
  not not_8 (not_8_out, in_2[2]);
  not not_9 (not_9_out, in_2[0]);
  not not_10 (not_10_out, in_1[1]);
  not not_11 (not_11_out, in_1[0]);
  not not_12 (not_12_out, in_2[2]);
  not not_13 (not_13_out, in_2[1]);
  not not_14 (not_14_out, in_1[1]);
  not not_15 (not_15_out, in_1[0]);
  not not_16 (not_16_out, in_2[2]);
  not not_17 (not_17_out, in_2[0]);
  not not_18 (not_18_out, in_1[1]);
  not not_19 (not_19_out, in_1[0]);
  not not_20 (not_20_out, in_2[1]);
  not not_21 (not_21_out, in_2[0]);
  not not_22 (not_22_out, in_1[2]);
  not not_23 (not_23_out, in_2[1]);
  not not_24 (not_24_out, in_2[0]);
  not not_25 (not_25_out, in_1[1]);
  not not_26 (not_26_out, in_1[0]);
  not not_27 (not_27_out, in_2[1]);
  not not_28 (not_28_out, in_2[0]);
  not not_29 (not_29_out, in_1[2]);
  not not_30 (not_30_out, in_1[0]);
  not not_31 (not_31_out, in_2[1]);
  not not_32 (not_32_out, in_2[0]);
  not not_33 (not_33_out, in_1[1]);
  not not_34 (not_34_out, in_1[0]);
  not not_35 (not_35_out, in_2[2]);
  not not_36 (not_36_out, in_2[0]);
  not not_37 (not_37_out, in_1[1]);
  not not_38 (not_38_out, in_1[0]);
  not not_39 (not_39_out, in_2[1]);
  not not_40 (not_40_out, in_2[0]);
  and and_1 (and_1_out, not_1_out, in_1[0], in_2[2], not_2_out, not_3_out);
  and and_2 (and_2_out, not_4_out, in_1[1], in_2[2], not_5_out, not_6_out);
  and and_3 (and_3_out, not_7_out, in_1[1], in_1[0], not_8_out, in_2[1], not_9_out);
  and and_4 (and_4_out, in_1[2], not_10_out, not_11_out, not_12_out, not_13_out, in_2[0]);
  and and_5 (and_5_out, in_1[2], not_14_out, not_15_out, not_16_out, in_2[1], not_17_out);
  and and_6 (and_6_out, in_1[2], not_18_out, not_19_out, in_2[2], not_20_out, not_21_out);
  and and_7 (and_7_out, not_22_out, in_1[1], in_1[0], in_2[2], not_23_out, not_24_out);
  and and_8 (and_8_out, in_1[2], not_25_out, not_26_out, in_2[2], not_27_out, not_28_out);
  and and_9 (and_9_out, not_29_out, in_1[1], not_30_out, in_2[2], not_31_out, not_32_out);
  and and_10 (and_10_out, in_1[2], not_33_out, not_34_out, not_35_out, in_2[1], not_36_out);
  and and_11 (and_11_out, in_1[2], not_37_out, not_38_out, in_2[2], not_39_out, not_40_out);
  or or_1 (sell, and_1_out, and_2_out, and_3_out, and_4_out, and_5_out, and_6_out);
  or or_2 (out_4[1], and_7_out, and_8_out);
  or or_3 (out_4[0], and_9_out, and_10_out, and_11_out);
endmodule
