// Logisim project test2.circ as structural Verilog: 1 circuit, main circuit ALU
module ALU (
  input  [31:0] i1,
  input  [31:0] i2,
  input  [3:0] in_3,
  output [31:0] result
);

  wire comparator_1_lt, comparator_2_lt;
  wire [2:0] bit_extender_1_out;
  wire [4:0] bitselector_1_out, bitselector_2_out, bitselector_3_out;
  wire [31:0] adder_1_out, and_1_out, and_2_out, and_3_out, bit_extender_2_out, bit_extender_3_out,
       divider_1_out, multiplier_1_out, not_1_out, not_2_out, not_3_out, or_1_out, or_2_out, or_3_out,
       shifter_1_out, shifter_2_out, shifter_3_out, subtractor_1_out;

  BitSelector #(.width(32), .group(5)) bitselector_1 (.in(i2), .out(bitselector_1_out), .sel(bit_extender_1_out));
  BitSelector #(.width(32), .group(5)) bitselector_2 (.in(i2), .out(bitselector_2_out), .sel(bit_extender_1_out));
  BitSelector #(.width(32), .group(5)) bitselector_3 (.in(i2), .out(bitselector_3_out), .sel(bit_extender_1_out));
  Multiplier #(.width(32)) multiplier_1 (.a(i1), .b(i2), .out(multiplier_1_out));  // open: cin, cout
  Divider #(.width(32)) divider_1 (.a(i1), .b(i2), .out(divider_1_out));  // open: upper, rem
  Adder #(.width(32)) adder_1 (.a(i1), .b(i2), .out(adder_1_out));  // open: cin, cout
  Subtractor #(.width(32)) subtractor_1 (.a(i1), .b(i2), .out(subtractor_1_out));  // open: bin, bout
  assign and_1_out = i1 & i2;  // AND_Gate and_1, 32 bits wide
  assign or_1_out = i1 | i2;  // OR_Gate or_1, 32 bits wide
  assign and_2_out = i1 & not_1_out;  // AND_Gate and_2, 32 bits wide
  assign not_1_out = ~i2;  // NOT_Gate not_1, 32 bits wide
  assign not_2_out = ~i1;  // NOT_Gate not_2, 32 bits wide
  assign and_3_out = not_2_out & i2;  // AND_Gate and_3, 32 bits wide
  assign or_2_out = i1 | i2;  // OR_Gate or_2, 32 bits wide
  Comparator #(.width(32)) comparator_1 (.a(i1), .b(i2), .lt(comparator_1_lt));  // open: gt, eq
  Comparator #(.width(32), .mode("unsigned")) comparator_2 (.a(i1), .b(i2), .lt(comparator_2_lt));  // open: gt, eq
  assign bit_extender_1_out = {{2{1'b0}}, 1'b0};  // Bit_Extender bit_extender_1
  Shifter #(.width(32)) shifter_1 (.in(i1), .\dist (bitselector_1_out), .out(shifter_1_out));
  Shifter #(.width(32), .shift("ar")) shifter_2 (.in(i1), .\dist (bitselector_2_out), .out(shifter_2_out));
  Shifter #(.width(32), .shift("lr")) shifter_3 (.in(i1), .\dist (bitselector_3_out), .out(shifter_3_out));
  assign or_3_out = and_2_out | and_3_out;  // OR_Gate or_3, 32 bits wide
  assign not_3_out = ~or_2_out;  // NOT_Gate not_3, 32 bits wide
  assign bit_extender_2_out = {{31{1'b0}}, comparator_1_lt};  // Bit_Extender bit_extender_2
  assign bit_extender_3_out = {{31{1'b0}}, comparator_2_lt};  // Bit_Extender bit_extender_3
  Multiplexer #(.select(4), .width(32), .enable("false")) multiplexer_1 (
    .in0(shifter_1_out), .in1(shifter_2_out), .in2(shifter_3_out), .in3(multiplier_1_out),
    .in4(divider_1_out), .in5(adder_1_out), .in6(subtractor_1_out), .in7(and_1_out), .in8(or_1_out),
    .in9(or_3_out), .in10(not_3_out), .in11(bit_extender_2_out), .in12(bit_extender_3_out), .out(result),
    .sel(in_3));  // open: in13, in14, in15
endmodule
