// Logisim project test3 (1).circ as structural Verilog: 2 circuits, main circuit transform
module xmod5 (
  input  in_1,
  output [2:0] out_2
);

  wire clock_1_out;
  wire [2:0] transform_1_out_3;

  Clock clock_1 (.out(clock_1_out));
  transform transform_1 (.\input (in_1), .in_2(out_2), .out_3(transform_1_out_3));
  Register #(.width(3)) register_1 (.D(transform_1_out_3), .Q(out_2), .clk(clock_1_out));  // open: en, clr
endmodule

module transform (
  input  \input ,
  input  [2:0] in_2,
  output [2:0] out_3
);

  wire and_1_out, and_2_out, and_3_out, and_4_out, and_5_out, and_6_out, and_7_out, and_8_out, not_1_out,
       not_2_out, not_3_out, not_4_out, not_5_out, not_6_out, not_7_out, not_8_out, not_9_out, not_10_out,
       not_11_out, not_12_out, not_13_out, not_14_out, not_15_out, not_16_out, not_17_out, not_18_out;

  not not_1 (not_1_out, \input );
  not not_2 (not_2_out, in_2[2]);
  not not_3 (not_3_out, in_2[0]);
  not not_4 (not_4_out, in_2[1]);
  not not_5 (not_5_out, in_2[0]);
  not not_6 (not_6_out, in_2[2]);
  not not_7 (not_7_out, in_2[1]);
  not not_8 (not_8_out, \input );
  not not_9 (not_9_out, in_2[1]);
  not not_10 (not_10_out, in_2[0]);
  not not_11 (not_11_out, in_2[2]);
  not not_12 (not_12_out, \input );
  not not_13 (not_13_out, in_2[2]);
  not not_14 (not_14_out, \input );
  not not_15 (not_15_out, in_2[1]);
  not not_16 (not_16_out, in_2[0]);
  not not_17 (not_17_out, in_2[2]);
  not not_18 (not_18_out, in_2[1]);
  and and_1 (and_1_out, not_1_out, not_2_out, in_2[1], not_3_out);
  and and_2 (and_2_out, \input , in_2[2], not_4_out, not_5_out);
  and and_3 (and_3_out, not_6_out, not_7_out, in_2[0]);
  and and_4 (and_4_out, not_8_out, in_2[2], not_9_out, not_10_out);
  and and_5 (and_5_out, \input , not_11_out, in_2[0]);
  and and_6 (and_6_out, not_12_out, not_13_out, in_2[1], in_2[0]);
  and and_7 (and_7_out, not_14_out, in_2[2], not_15_out, not_16_out);
  and and_8 (and_8_out, \input , not_17_out, not_18_out);
  or or_1 (out_3[2], and_1_out, and_2_out);
  or or_2 (out_3[1], and_3_out, and_4_out, and_5_out);
  or or_3 (out_3[0], and_6_out, and_7_out, and_8_out);
endmodule
